# Fritzing sketch ascchw_rev2 (saved by Fritzing 0.9.3b)
stripboards: 1

parts:
  Nano1 = Arduino Nano v2.3
  Q1 = Basic FET N-Channel [package="TO220 [THT]"]
  Q2 = Basic FET N-Channel [package="TO220 [THT]"]
  Q3 = Basic FET N-Channel [package="TO220 [THT]"]
  Q4 = Basic FET N-Channel [package="TO220 [THT]"]
  R5 = Resistor [tolerance=±5% resistance=220 package="2512 [SMD]"]
  R6 = Resistor [tolerance=±5% resistance=220 package="2512 [SMD]"]
  R7 = Resistor [tolerance=±5% resistance=220 package="2512 [SMD]"]
  R8 = Resistor [tolerance=±5% resistance=220 package="2512 [SMD]"]

nets:
  N1: Nano1.GND, Q1.source, Q2.source, Q3.source, Q4.source, R5.Pin_1, R6.Pin_1, R7.Pin_1, R8.Pin_1
  N2: Nano1.D2, Q1.gate
  N3: Nano1.D3, Q3.gate
  N4: Nano1.D6, Q2.gate
  N5: Nano1.D12, Q4.gate
  N6: Q1.drain, R8.Pin_0
  N7: Q2.drain, R6.Pin_0
  N8: Q3.drain, R7.Pin_0
  N9: Q4.drain, R5.Pin_0
